# Fritzing sketch led (saved by Fritzing 0.9.3b)
breadboards: 2

parts:
  Composant1 = Arduino Uno (Rev3)
  HEF1 = HEF4094 [package="DIP16 [THT]"]
  HEF2 = HEF4094 [package="DIP16 [THT]"]
  LED1 = LED - 5mm [color="Red (633nm)" package="5 mm [THT]"]
  LED2 = LED - 5mm [color="Red (633nm)" package="5 mm [THT]"]
  LED3 = LED - 5mm [color="Red (633nm)" package="5 mm [THT]"]
  LED4 = LED - 5mm [color="Red (633nm)" package="5 mm [THT]"]
  LED5 = LED - 5mm [color="Red (633nm)" package="5 mm [THT]"]
  LED6 = LED - 5mm [color="Red (633nm)" package="5 mm [THT]"]
  LED7 = LED - 5mm [color="Red (633nm)" package="5 mm [THT]"]
  LED8 = LED - 5mm [color="Red (633nm)" package="5 mm [THT]"]
  R1 = Resistor [tolerance=±5% resistance=220 package=THT]
  R2 = Resistor [tolerance=±5% resistance=220 package=THT]
  R3 = Resistor [tolerance=±5% resistance=220 package=THT]
  R4 = Resistor [tolerance=±5% resistance=220 package=THT]
  R5 = Resistor [tolerance=±5% resistance=220 package=THT]
  R6 = Resistor [tolerance=±5% resistance=220 package=THT]
  R7 = Resistor [tolerance=±5% resistance=220 package=THT]
  R8 = Resistor [tolerance=±5% resistance=220 package=THT]
  S1 = Pushbutton [package="[THT]"]
  R9 = Resistor [tolerance=±5% resistance=220 package=THT]  # not connected

nets:
  N1: Composant1.D8, HEF1.STROBE, HEF2.STROBE
  N2: Composant1.D11_PWM/MOSI, HEF1.DATA
  VSS: Composant1.GND, HEF1.Vss, HEF2.Vss, R1.Pin_0, R2.Pin_0, R3.Pin_0, R4.Pin_0, R5.Pin_0, R6.Pin_0, R7.Pin_0, R8.Pin_0
  VDD: Composant1.5V, HEF1.OE, HEF1.Vdd, HEF2.OE, HEF2.Vdd, S1.Pin_1, S1.Pin_2, S1.Pin_3, S1.Pin_4
  N3: HEF1.CLOCK, HEF2.CLOCK
  N4: HEF1.Q1, LED4.anode
  N5: HEF1.Q2, LED3.anode
  N6: HEF1.Q3, LED2.anode
  N7: HEF1.Q4, LED1.anode
  N8: HEF1.Q's, HEF2.DATA
  N9: HEF2.Q1, LED8.anode
  N10: HEF2.Q2, LED7.anode
  N11: HEF2.Q3, LED6.anode
  N12: HEF2.Q4, LED5.anode
